// Logisim project Ekran.circ as structural Verilog: 1 circuit, main circuit main
module main (
);

  wire clock_1_out, keyboard_1_avail, main_2_p2, main_2_p3, main_2_p4, register_1_q;
  wire [4:0] main_1_out_2, main_1_out_3;
  wire [6:0] keyboard_1_data;
  wire [31:0] adder_1_out, main_3_p3, main_3_p4, main_3_p5, main_3_p6, main_3_p7, main_3_p8, main_3_p9,
       main_3_p10, main_3_p11, main_3_p12, main_3_p13, main_3_p14, main_3_p15, main_3_p16, main_3_p17,
       main_3_p18, main_3_p19, main_3_p20, main_3_p21, main_3_p22, main_3_p23, main_3_p24, main_3_p25,
       main_3_p26, main_3_p27, main_3_p28, main_3_p29, main_3_p30, main_3_p31, main_3_p32, main_3_p33,
       main_3_p34, main_4_out_35, main_4_out_36, main_4_out_37, main_4_out_38, main_4_out_39, main_4_out_40,
       main_4_out_41, main_4_out_42, main_4_out_43, main_4_out_44, main_4_out_45, main_4_out_46,
       main_4_out_47, main_4_out_48, main_4_out_49, main_4_out_50, main_4_out_51, main_4_out_52,
       main_4_out_53, main_4_out_54, main_4_out_55, main_4_out_56, main_4_out_57, main_4_out_58,
       main_4_out_59, main_4_out_60, main_4_out_61, main_4_out_62, main_4_out_63, main_4_out_64,
       main_4_out_65, main_4_out_66, shifter_1_out, shifter_2_out;

  Keyboard keyboard_1 (.re(1'b1), .clr(register_1_q), .avail(keyboard_1_avail), .data(keyboard_1_data));  // open: clk
  Clock clock_1 (.out(clock_1_out));
  Register #(.width(1)) register_1 (.D(keyboard_1_avail), .Q(register_1_q), .clk(clock_1_out));  // open: en, clr
  Register #(.width(7)) register_2 (.D(keyboard_1_data), .clk(clock_1_out));  // open: en, Q, clr
  LR_main main_1 (.in_1(keyboard_1_data), .out_2(main_1_out_2), .out_3(main_1_out_3));
  // Enter_Up_Down_main main_2: pin names not known; wires that end beside it: keyboard_1_data, main_2_p2, main_2_p3, main_2_p4
  Shifter #(.width(32)) shifter_1 (.in(32'h8000), .\dist (main_1_out_2), .out(shifter_1_out));
  Shifter #(.width(32), .shift("lr")) shifter_2 (.in(shifter_1_out), .\dist (main_1_out_3), .out(shifter_2_out));
  Adder #(.width(32)) adder_1 (.a({32{1'b0}}), .b(shifter_2_out), .out(adder_1_out));  // open: cin, cout
  // Uu_Down32_main main_3: pin names not known; wires that end beside it: main_2_p3, adder_1_out, main_3_p3, main_3_p4, main_3_p5, main_3_p6, main_3_p7, main_3_p8, main_3_p9, main_3_p10, main_3_p11, main_3_p12, main_3_p13, main_3_p14, main_3_p15, main_3_p16, main_3_p17, main_3_p18, main_3_p19, main_3_p20, main_3_p21, main_3_p22, main_3_p23, main_3_p24, main_3_p25, main_3_p26, main_3_p27, main_3_p28, main_3_p29, main_3_p30, main_3_p31, main_3_p32, main_3_p33, main_3_p34
  DotMatrix #(.inputtype("row"), .matrixcols(32), .matrixrows(32)) dotmatrix_1 (
    .row0(main_4_out_35), .row1(main_4_out_36), .row2(main_4_out_37), .row3(main_4_out_38),
    .row4(main_4_out_39), .row5(main_4_out_40), .row6(main_4_out_41), .row7(main_4_out_42),
    .row8(main_4_out_46), .row9(main_4_out_45), .row10(main_4_out_44), .row11(main_4_out_43),
    .row12(main_4_out_50), .row13(main_4_out_49), .row14(main_4_out_48), .row15(main_4_out_47),
    .row16(main_4_out_58), .row17(main_4_out_57), .row18(main_4_out_56), .row19(main_4_out_55),
    .row20(main_4_out_54), .row21(main_4_out_53), .row22(main_4_out_52), .row23(main_4_out_51),
    .row24(main_4_out_66), .row25(main_4_out_65), .row26(main_4_out_64), .row27(main_4_out_63),
    .row28(main_4_out_62), .row29(main_4_out_61), .row30(main_4_out_60), .row31(main_4_out_59));
  Register32x32_main main_4 (
    .in_1(main_2_p2), .in_2(main_3_p3), .in_3(main_3_p27), .in_4(main_3_p19), .in_5(main_3_p15),
    .in_6(main_3_p11), .in_7(main_3_p7), .in_8(main_3_p4), .in_9(main_3_p28), .in_10(main_3_p20),
    .in_11(main_3_p16), .in_12(main_3_p12), .in_13(main_3_p8), .in_14(main_3_p5), .in_15(main_3_p29),
    .in_16(main_3_p21), .in_17(main_3_p17), .in_18(main_3_p13), .in_19(main_3_p9), .in_20(main_3_p6),
    .in_21(main_3_p30), .in_22(main_3_p22), .in_23(main_3_p18), .in_24(main_3_p14), .in_25(main_3_p10),
    .in_26(main_3_p31), .in_27(main_3_p23), .in_28(main_3_p32), .in_29(main_3_p24), .in_30(main_3_p33),
    .in_31(main_3_p25), .in_32(main_3_p34), .in_33(main_3_p26), .out_35(main_4_out_35),
    .out_36(main_4_out_36), .out_37(main_4_out_37), .out_38(main_4_out_38), .out_39(main_4_out_39),
    .out_40(main_4_out_40), .out_41(main_4_out_41), .out_42(main_4_out_42), .out_43(main_4_out_43),
    .out_44(main_4_out_44), .out_45(main_4_out_45), .out_46(main_4_out_46), .out_47(main_4_out_47),
    .out_48(main_4_out_48), .out_49(main_4_out_49), .out_50(main_4_out_50), .out_51(main_4_out_51),
    .out_52(main_4_out_52), .out_53(main_4_out_53), .out_54(main_4_out_54), .out_55(main_4_out_55),
    .out_56(main_4_out_56), .out_57(main_4_out_57), .out_58(main_4_out_58), .out_59(main_4_out_59),
    .out_60(main_4_out_60), .out_61(main_4_out_61), .out_62(main_4_out_62), .out_63(main_4_out_63),
    .out_64(main_4_out_64), .out_65(main_4_out_65), .out_66(main_4_out_66), .in_34(main_2_p4));
endmodule
