// Logisim project Uu_Down32.circ as structural Verilog: 1 circuit, main circuit main
module main (
  input  [4:0] in_1,
  input  [19:0] in_2,
  input  in_3,
  output [19:0] out_4,
  output [19:0] out_5,
  output [19:0] out_6,
  output [19:0] out_7,
  output [19:0] out_8,
  output [19:0] out_9,
  output [19:0] out_10,
  output [19:0] out_11,
  output [19:0] out_12,
  output [19:0] out_13,
  output [19:0] out_14,
  output [19:0] out_15,
  output [19:0] out_16,
  output [19:0] out_17,
  output [19:0] out_18,
  output [19:0] out_19,
  output [19:0] out_20,
  output [19:0] out_21,
  output [19:0] out_22,
  output [19:0] out_23
);

  Uu_Down1_main main_1 (.in_1(in_2), .in_2(in_1), .in_3(5'b10011), .in_4(in_3), .out_5(out_4));
  Uu_Down1_main main_2 (.in_1(in_2), .in_2(in_1), .in_3(5'b10010), .in_4(in_3), .out_5(out_5));
  Uu_Down1_main main_3 (.in_1(in_2), .in_2(in_1), .in_3(5'b10001), .in_4(in_3), .out_5(out_6));
  Uu_Down1_main main_4 (.in_1(in_2), .in_2(in_1), .in_3(5'b10000), .in_4(in_3), .out_5(out_7));
  Uu_Down1_main main_5 (.in_1(in_2), .in_2(in_1), .in_3(5'b01111), .in_4(in_3), .out_5(out_8));
  Uu_Down1_main main_6 (.in_1(in_2), .in_2(in_1), .in_3(5'b01110), .in_4(in_3), .out_5(out_9));
  Uu_Down1_main main_7 (.in_1(in_2), .in_2(in_1), .in_3(5'b01101), .in_4(in_3), .out_5(out_10));
  Uu_Down1_main main_8 (.in_1(in_2), .in_2(in_1), .in_3(5'b01100), .in_4(in_3), .out_5(out_11));
  Uu_Down1_main main_9 (.in_1(in_2), .in_2(in_1), .in_3(5'b01011), .in_4(in_3), .out_5(out_12));
  Uu_Down1_main main_10 (.in_1(in_2), .in_2(in_1), .in_3(5'b01010), .in_4(in_3), .out_5(out_13));
  Uu_Down1_main main_11 (.in_1(in_2), .in_2(in_1), .in_3(5'b01001), .in_4(in_3), .out_5(out_14));
  Uu_Down1_main main_12 (.in_1(in_2), .in_2(in_1), .in_3(5'b01000), .in_4(in_3), .out_5(out_15));
  Uu_Down1_main main_13 (.in_1(in_2), .in_2(in_1), .in_3(5'b00111), .in_4(in_3), .out_5(out_16));
  Uu_Down1_main main_14 (.in_1(in_2), .in_2(in_1), .in_3(5'b00110), .in_4(in_3), .out_5(out_17));
  Uu_Down1_main main_15 (.in_1(in_2), .in_2(in_1), .in_3(5'b00101), .in_4(in_3), .out_5(out_18));
  Uu_Down1_main main_16 (.in_1(in_2), .in_2(in_1), .in_3(5'b00100), .in_4(in_3), .out_5(out_19));
  Uu_Down1_main main_17 (.in_1(in_2), .in_2(in_1), .in_3(5'b00011), .in_4(in_3), .out_5(out_20));
  Uu_Down1_main main_18 (.in_1(in_2), .in_2(in_1), .in_3(5'b00010), .in_4(in_3), .out_5(out_21));
  Uu_Down1_main main_19 (.in_1(in_2), .in_2(in_1), .in_3(5'b00001), .in_4(in_3), .out_5(out_22));
  Uu_Down1_main main_20 (.in_1(in_2), .in_2(in_1), .in_3({5{1'b0}}), .in_4(in_3), .out_5(out_23));
endmodule
